# Fritzing sketch ESQUEMA (saved by Fritzing 0.9.10b)
breadboards: 2

parts:
  J1 = Basic Servo
  J2 = Basic Servo
  J3 = Basic Servo
  Componente1 = Arduino Uno (Rev3)
  MOTOR1 = 28BYJ-48 Stepper Motor  # not connected
  Driver2 = 28BYJ-48 Driver Module [part_number=ULN2003 package=THT]
  SW1 = ENCODER_RGB_CA [package=encoder_led_3]
  R1 = Trimmer Potentiometer [maximum_resistance=10kΩ knob_status=50% power=0.5W package=THT]
  R2 = Trimmer Potentiometer [maximum_resistance=10kΩ knob_status=50% power=0.5W package=THT]
  R3 = Trimmer Potentiometer [maximum_resistance=10kΩ knob_status=50% power=0.5W package=THT]

nets:
  GND: J1.gnd, J2.gnd, J3.gnd, Driver2.GND, SW1.-B
  VCC: J1.vcc, J2.vcc, J3.vcc, Driver2.Vmotor, SW1.+
  N1: J1.pulse, Componente1.D7
  N2: J2.pulse, Componente1.D4
  N3: J3.pulse, Componente1.D2
  N4: Componente1.A1, R1.wiper
  N5: Componente1.A2, R2.wiper
  N6: Componente1.A3, R3.wiper
  N7: Componente1.A4/SDA, SW1.C
  N8: Componente1.A5/SCL, SW1.B
  N9: Componente1.D8, Driver2.IN4
  N10: Componente1.D9_PWM, Driver2.IN3
  N11: Componente1.D10_PWM/SS, Driver2.IN2
  N12: Componente1.D11_PWM/MOSI, Driver2.IN1
  N13: Componente1.5V, R1.leg1, R2.leg1, R3.leg1
  N14: Componente1.GND, R1.leg2, R2.leg2, R3.leg2

custom parts:
  28BYJ-48 Driver Module: Generic male header
